# Fritzing sketch esp32_motion_sensor_oled (saved by Fritzing 0.9.3b)

parts:
  M1 = DOIT Esp32 DevKit v1 (30 pins long, 11 pins width) [part_number=ESP32S-PIN30]
  PIR_HC-SR501 = HC-SR501 Body Sensor Module
  OLED2 = OLED 128x64 I2C Monochrome Display
  R1 = Resistor [tolerance=±5% resistance=10k package="0805 [SMD]"]

nets:
  3V3: M1.3V3, OLED2.VDD
  GND: M1.GND, PIR_HC-SR501.GND, OLED2.GND, R1.Pin_0
  N1: M1.D21, OLED2.SDA
  N2: M1.D22, OLED2.SCK
  N3: M1.D34, PIR_HC-SR501.OUT, R1.Pin_1
  VIN: M1.VIN, PIR_HC-SR501.VCC

custom parts:
  DOIT Esp32 DevKit v1 (30 pins long, 11 pins width): The DOIT Esp32 DevKit v1 is one of the development board created by DOIT to evaluate the ESP-WROOM-32 module. It is based on the ESP32 microcontroller that boasts Wifi, Bluetooth, Ethernet and Low Power support all in a single chip. (vanepp) made breadboard work, adjusted pin numbering and labels and reduced size of schematic and cleaned up pcb. This chip is 30pins long (2 x15) and 11 pins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
  HC-SR501 Body Sensor Module: Pyroelectric Infrared PIR Motion Sensor Detector Module
